# Fritzing sketch vl53l1x_scanner (saved by Fritzing 0.9.3b)

parts:
  Part1 = Arduino Uno (Rev3) - ICSP
  Part2 = Adafruit VL53L0X Time of Flight Distance Sensor [part_number="Adafruit #3317"]
  BREAKOUT1 = ULN2003A breakout board
  MOTOR2 = 28BYJ-48 Stepper Motor

nets:
  N1: Part1.D9_PWM, BREAKOUT1.In_1
  N2: Part1.D10_PWM/SS, BREAKOUT1.In_2
  N3: Part1.D11_PWM/MOSI, BREAKOUT1.In_3
  N4: Part1.D12/MISO, BREAKOUT1.In_4
  N5: Part1.A4/SDA, Part2.SCL
  N6: Part1.A5/SCL, Part2.SDA
  5V: Part1.5V, Part2.VIN
  GND: Part1.GND, Part2.GND
  N7: BREAKOUT1.RED_wire, MOTOR2.YELLOW
  N8: BREAKOUT1.ORANGE_wire, MOTOR2.ORANGE
  N9: BREAKOUT1.YELLOW_wire, MOTOR2.RED
  N10: BREAKOUT1.PINK_wire, MOTOR2.PINK
  N11: BREAKOUT1.BLUE_wire, MOTOR2.BLUE

custom parts:
  Adafruit VL53L0X Time of Flight Distance Sensor: The VL53L0X is a Time of Flight distance sensor like no other you've used! The sensor contains a very tiny invisible laser source, and a matching sensor. The VL53L0X can detect the "time of flight", or how long the light has taken to bounce back to the sensor. Since it uses a very narrow light source, it is good for determining distance of only the surface directly in front of it. Unlike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
  ULN2003A breakout board: ULN2003A 7-way Darlington Transistor Driver on breakoutboard
  28BYJ-48 Stepper Motor: 28BYJ-48 gear-reduction stepper motor (small)
